# Fritzing sketch Connections (saved by Fritzing 0.9.3b)
breadboards: 1

parts:
  R2 = Resistor [tolerance=±5% resistance=220 package="2512 [SMD]"]
  MKRGSM1 = Arduino MKR GSM 1400
  BREAKOUT1 = MAX31850_Thermocouple_Breakout

nets:
  N1: R2.Pin_0, MKRGSM1.D2_PWM, BREAKOUT1.connector8
  N2: R2.Pin_1, MKRGSM1.7, BREAKOUT1.connector3
  N3: MKRGSM1.GND, BREAKOUT1.connector1
